// Logisim project 4-1mux.circ as structural Verilog: 2 circuits, main circuit 4-1mux
module _4_1mux (
  input  in_1,
  input  in_2,
  input  in_3,
  input  in_4,
  input  in_5,
  input  in_6,
  output out_7
);

  wire nand_1_out, nand_2_out, nand_3_out, nand_4_out, nand_5_out, nand_6_out;

  nand nand_1 (nand_1_out, in_5, in_5);
  nand nand_2 (nand_2_out, in_6, in_6);
  nand nand_3 (nand_3_out, in_1, nand_1_out, nand_2_out);
  nand nand_4 (nand_4_out, in_2, nand_1_out, in_6);
  nand nand_5 (nand_5_out, in_3, nand_2_out, in_5, in_5);
  nand nand_6 (nand_6_out, in_4, in_4, in_5, in_6);
  nand nand_7 (out_7, nand_3_out, nand_4_out, nand_5_out, nand_6_out);
endmodule

module main (
  input  in_1,
  input  in_2,
  input  in_3,
  input  in_4,
  input  in_5,
  input  in_6,
  input  in_7,
  input  in_8,
  output out_9
);

  wire n4_1mux_1_out_7, n4_1mux_2_out_7;

  _4_1mux u_4_1mux_1 (.in_1(in_1), .in_2(in_2), .in_3(in_3), .in_4(in_4), .out_7(n4_1mux_1_out_7));  // open: in_5, in_6
  _4_1mux u_4_1mux_2 (.in_1(in_5), .in_2(in_6), .in_3(in_7), .in_4(in_8), .out_7(n4_1mux_2_out_7));  // open: in_5, in_6
  xor xor_1 (out_9, n4_1mux_1_out_7, n4_1mux_2_out_7);
endmodule
