// Logisim project 8bit-alu.circ as structural Verilog: 2 circuits, main circuit 1bit
module _1bit (
  input  in_1,
  input  in_2,
  input  [1:0] in_3,
  output out_4
);

  wire and_1_out, not_1_out, or_1_out;

  not not_1 (not_1_out, in_1);
  or or_1 (or_1_out, in_1, in_2);
  and and_1 (and_1_out, in_1, in_2);
  Multiplexer #(.select(2)) multiplexer_1 (
    .in0(not_1_out), .in1(or_1_out), .in2(and_1_out), .out(out_4), .sel(in_3));  // open: in3, en
endmodule

module _8bit (
  input  [7:0] in_1,
  input  [1:0] in_2,
  input  [7:0] in_3,
  output [7:0] out_4
);

  _1bit u_1bit_1 (.in_1(in_1[0]), .in_2(in_3[7]), .in_3(in_2), .out_4(out_4[0]));
  _1bit u_1bit_2 (.in_1(in_1[1]), .in_2(in_3[6]), .in_3(in_2), .out_4(out_4[1]));
  _1bit u_1bit_3 (.in_1(in_1[2]), .in_2(in_3[5]), .in_3(in_2), .out_4(out_4[2]));
  _1bit u_1bit_4 (.in_1(in_1[3]), .in_2(in_3[4]), .in_3(in_2), .out_4(out_4[3]));
  _1bit u_1bit_5 (.in_1(in_1[4]), .in_2(in_3[3]), .in_3(in_2), .out_4(out_4[4]));
  _1bit u_1bit_6 (.in_1(in_1[5]), .in_2(in_3[2]), .in_3(in_2), .out_4(out_4[5]));
  _1bit u_1bit_7 (.in_1(in_1[6]), .in_2(in_3[1]), .in_3(in_2), .out_4(out_4[6]));
  _1bit u_1bit_8 (.in_1(in_1[7]), .in_2(in_3[0]), .in_3(in_2), .out_4(out_4[7]));
endmodule
